# Fritzing sketch PrototypeCircuit (saved by Fritzing 0.9.5d)
circuit board: 8.37488cm x 3.89172cm

parts:
  WeMos_D1_Mini_TX = WeMos D1 Mini
  WeMos_D1_Mini_RX = WeMos D1 Mini
  S1 = Pushbutton [package="[THT]"]
  R2 = Resistor [tolerance=±5% resistance=100 package=THT]
  R1 = Resistor [tolerance=±5% resistance=10k package=THT]
  LED1 = LED - 5mm [color="Red (633nm)" package="5 mm [THT]"]

nets:
  N1: WeMos_D1_Mini_TX.3V3, R1.Pin_1
  N2: WeMos_D1_Mini_TX.D5, S1.Pin_1, R1.Pin_0
  N3: WeMos_D1_Mini_TX.G, S1.Pin_3, S1.Pin_4
  N4: WeMos_D1_Mini_RX.D4, R2.Pin_1
  N5: WeMos_D1_Mini_RX.G, LED1.anode
  N6: R2.Pin_0, LED1.cathode

custom parts:
  WeMos D1 Mini: The D1 mini is a mini wifi board based on ESP-8266EX.
